# Fritzing sketch esp-12f-battery-powered (saved by Fritzing 0.9.4)
circuit board: 5.2cm x 3.6cm
breadboards: 1

parts:
  S1_RESET = Pushbutton [package="[THT]"]
  R2 = Resistor [tolerance=±5% resistance=10k package=THT]
  R5 = Resistor [tolerance=±5% resistance=10k package=THT]
  R6 = Resistor [tolerance=±5% resistance=10k package=THT]
  R7 = Resistor [tolerance=±5% resistance=10k package=THT]
  R8 = Resistor [tolerance=±5% resistance=10k package=THT]
  R9 = Resistor [tolerance=±5% resistance=10k package=THT]
  ESP-12F = Gizwits WiFi Witty ESP-12F

nets:
  GND: S1_RESET.Pin_1, S1_RESET.Pin_2, R8.Pin_1, ESP-12F.GND
  REST: S1_RESET.Pin_3, S1_RESET.Pin_4, R2.Pin_1, ESP-12F.REST
  3.3V: R2.Pin_0, R5.Pin_0, R6.Pin_1, R7.Pin_1, R9.Pin_1, ESP-12F.VCC
  N1: R5.Pin_1, ESP-12F.CH_PD
  GPIO0: R6.Pin_0, ESP-12F.GPIO0
  GPIO2: R7.Pin_0, ESP-12F.GPIO2
  N2: R8.Pin_0, ESP-12F.GPIO15
  GPIO4: R9.Pin_0, ESP-12F.GPIO4
